// Logisim project trabIsa12bits.circ as structural Verilog: 4 circuits, main circuit main
module main (
);

  wire bzrz, clk, comparator_1_eq, comparator_1_gt, muxULA, or_1_out, sel_lw_1_out_3, wBreg, wRAM;
  wire [1:0] mux_pc, muxReg;
  wire [3:0] opcode;
  wire [7:0] rom_2_data;
  wire [11:0] A, adder_2_out, adder_3_out, B, imm, multiplexer_1_out, multiplexer_2_out, multiplexer_3_out,
       multiplexer_4_out, multiplexer_5_out, multiplexer_6_out, PC_q, pcM1, ram_1_dout, ula_1_c;

  Multiplexer #(.width(12)) multiplexer_1 (
    .in0(12'h1), .in1({12{1'b0}}), .out(multiplexer_1_out), .sel(sel_lw_1_out_3));
  Clock clock_1 (.out(clk));
  sel_lw sel_lw_1 (.mux_reg(muxReg), .clk(clk), .out_3(sel_lw_1_out_3));
  Adder #(.width(12)) adder_1 (.a(PC_q), .b(multiplexer_1_out), .out(pcM1));  // open: cin, cout
  Adder #(.width(12)) adder_2 (.a(PC_q), .b(imm), .out(adder_2_out));  // open: cin, cout
  Multiplexer #(.width(12)) multiplexer_2 (.in0(pcM1), .in1(B), .out(multiplexer_2_out), .sel(bzrz));
  Adder #(.width(12)) adder_3 (.a(A), .b(imm), .out(adder_3_out));  // open: cin, cout
  // Probe on opcode
  ROM #(.addrWidth(4), .dataWidth(7)) rom_1 (.addr(opcode), .data({mux_pc, wBreg, muxULA, muxReg, wRAM}));
  Multiplexer #(.select(2), .width(12)) multiplexer_3 (
    .in0(pcM1), .in1(adder_2_out), .in2(adder_3_out), .in3(multiplexer_2_out), .out(multiplexer_3_out),
    .sel(mux_pc));
  Register #(.width(12)) PC (.D(multiplexer_3_out), .en(1'b1), .clk(clk), .Q(PC_q));  // open: clr
  // Probe on {mux_pc, wBreg, muxULA, muxReg, wRAM}
  ROM #(.addrWidth(12), .dataWidth(12)) rom_2 (.addr(PC_q), .data({opcode, rom_2_data}));
  assign imm = {{8{rom_2_data[3]}}, rom_2_data[3:0]};  // Bit_Extender bit_extender_1
  Multiplexer #(.select(2), .width(12)) multiplexer_4 (
    .in0(ula_1_c), .in1(ram_1_dout), .in2(multiplexer_5_out), .in3(pcM1), .out(multiplexer_4_out),
    .sel(muxReg));
  // Probe on muxReg
  bancoReg bancoreg_1 (
    .D(multiplexer_4_out), .rs1(rom_2_data[7:4]), .rs2(rom_2_data[3:0]), .rd(rom_2_data[7:4]), .WE(wBreg),
    .CLK(clk), .a(A), .b(B));
  Multiplexer #(.width(12)) multiplexer_5 (.in0(12'h1), .in1({12{1'b0}}), .out(multiplexer_5_out), .sel(or_1_out));
  or or_1 (or_1_out, comparator_1_gt, comparator_1_eq);
  Comparator #(.width(12)) comparator_1 (.a(A), .b(B), .gt(comparator_1_gt), .eq(comparator_1_eq));  // open: lt
  Multiplexer #(.width(12)) multiplexer_6 (.in0(B), .in1(imm), .out(multiplexer_6_out), .sel(muxULA));
  ula ula_1 (.A(A), .B(multiplexer_6_out), .OPULA(opcode), .Ra_igual_0(bzrz), .C(ula_1_c));
  // Probe on B
  RAM #(.addrWidth(12), .dataWidth(12)) ram_1 (.addr(B), .we(wRAM), .oe(1'b1), .clk(clk), .din(A), .dout(ram_1_dout));
  // Probe on ram_1_dout

  // Other names for the same wires on the sheet: opULA[3:0] = opcode

  // Notes on the sheet:
  //   contents of rom_1 (hex, n*v repeats v):
  //   10 18 36 56 60 14 1 12 7*10
  //   contents of rom_2 (hex, n*v repeats v):
  //   40 10 155 155 1f5 9ff 1f2 25 32 33 64 565 46f 71 74 647 75 85 884 687 141 866 877 888 8dd d5 3d0 844
  //   1fe 1e1 afe 2e1 64 565 46f 74 787 75 797 75 89 687 141 866 877 3ef
endmodule

module bancoReg (
  input  [11:0] D,
  input  [3:0] rs1,
  input  [3:0] rs2,
  input  [3:0] rd,
  input  WE,
  input  CLK,
  output [11:0] a,
  output [11:0] b
);

  wire demultiplexer_1_out0, demultiplexer_1_out1, demultiplexer_1_out2, demultiplexer_1_out3,
       demultiplexer_1_out4, demultiplexer_1_out5, demultiplexer_1_out6, demultiplexer_1_out7,
       demultiplexer_1_out8, demultiplexer_1_out9, demultiplexer_1_out10, demultiplexer_1_out11,
       demultiplexer_1_out12, demultiplexer_1_out13, demultiplexer_1_out14, demultiplexer_1_out15;
  wire [11:0] multiplexer_1_out, multiplexer_2_out, multiplexer_3_out, multiplexer_4_out, multiplexer_5_out,
       multiplexer_6_out, multiplexer_7_out, multiplexer_8_out, multiplexer_9_out, multiplexer_10_out,
       multiplexer_11_out, multiplexer_12_out, multiplexer_13_out, multiplexer_14_out, multiplexer_15_out,
       r1, r2, r3, r4, r5, r6, r7, r8, r9, r10, r11, r12, r13, r14, r15;

  // NoConnect on demultiplexer_1_out0
  Demultiplexer #(.select(4)) demultiplexer_1 (
    .out0(demultiplexer_1_out0), .out1(demultiplexer_1_out1), .out2(demultiplexer_1_out2),
    .out3(demultiplexer_1_out3), .out4(demultiplexer_1_out4), .out5(demultiplexer_1_out5),
    .out6(demultiplexer_1_out6), .out7(demultiplexer_1_out7), .out8(demultiplexer_1_out8),
    .out9(demultiplexer_1_out9), .out10(demultiplexer_1_out10), .out11(demultiplexer_1_out11),
    .out12(demultiplexer_1_out12), .out13(demultiplexer_1_out13), .out14(demultiplexer_1_out14),
    .out15(demultiplexer_1_out15), .in(WE), .sel(rd));
  Register #(.width(12)) u_r1 (.D(multiplexer_1_out), .clk(CLK), .Q(r1));  // open: en, clr
  Multiplexer #(.width(12)) multiplexer_1 (.in0(r1), .in1(D), .out(multiplexer_1_out), .sel(demultiplexer_1_out1));
  Register #(.width(12)) u_r2 (.D(multiplexer_2_out), .clk(CLK), .Q(r2));  // open: en, clr
  Multiplexer #(.width(12)) multiplexer_2 (.in0(r2), .in1(D), .out(multiplexer_2_out), .sel(demultiplexer_1_out2));
  Register #(.width(12)) u_r3 (.D(multiplexer_3_out), .clk(CLK), .Q(r3));  // open: en, clr
  Multiplexer #(.width(12)) multiplexer_3 (.in0(r3), .in1(D), .out(multiplexer_3_out), .sel(demultiplexer_1_out3));
  Register #(.width(12)) u_r4 (.D(multiplexer_4_out), .clk(CLK), .Q(r4));  // open: en, clr
  Multiplexer #(.width(12)) multiplexer_4 (.in0(r4), .in1(D), .out(multiplexer_4_out), .sel(demultiplexer_1_out4));
  Register #(.width(12)) u_r5 (.D(multiplexer_5_out), .clk(CLK), .Q(r5));  // open: en, clr
  Multiplexer #(.width(12)) multiplexer_5 (.in0(r5), .in1(D), .out(multiplexer_5_out), .sel(demultiplexer_1_out5));
  Register #(.width(12)) u_r6 (.D(multiplexer_6_out), .clk(CLK), .Q(r6));  // open: en, clr
  Multiplexer #(.width(12)) multiplexer_6 (.in0(r6), .in1(D), .out(multiplexer_6_out), .sel(demultiplexer_1_out6));
  Register #(.width(12)) u_r7 (.D(multiplexer_7_out), .clk(CLK), .Q(r7));  // open: en, clr
  Multiplexer #(.width(12)) multiplexer_7 (.in0(r7), .in1(D), .out(multiplexer_7_out), .sel(demultiplexer_1_out7));
  Register #(.width(12)) u_r8 (.D(multiplexer_8_out), .clk(CLK), .Q(r8));  // open: en, clr
  Multiplexer #(.width(12)) multiplexer_8 (.in0(r8), .in1(D), .out(multiplexer_8_out), .sel(demultiplexer_1_out8));
  Register #(.width(12)) u_r9 (.D(multiplexer_9_out), .clk(CLK), .Q(r9));  // open: en, clr
  Multiplexer #(.width(12)) multiplexer_9 (.in0(r9), .in1(D), .out(multiplexer_9_out), .sel(demultiplexer_1_out9));
  Register #(.width(12)) u_r10 (.D(multiplexer_10_out), .clk(CLK), .Q(r10));  // open: en, clr
  Multiplexer #(.width(12)) multiplexer_10 (.in0(r10), .in1(D), .out(multiplexer_10_out), .sel(demultiplexer_1_out10));
  Register #(.width(12)) u_r11 (.D(multiplexer_11_out), .clk(CLK), .Q(r11));  // open: en, clr
  Multiplexer #(.width(12)) multiplexer_11 (.in0(r11), .in1(D), .out(multiplexer_11_out), .sel(demultiplexer_1_out11));
  Register #(.width(12)) u_r12 (.D(multiplexer_12_out), .clk(CLK), .Q(r12));  // open: en, clr
  Multiplexer #(.width(12)) multiplexer_12 (.in0(r12), .in1(D), .out(multiplexer_12_out), .sel(demultiplexer_1_out12));
  Register #(.width(12)) u_r13 (.D(multiplexer_13_out), .clk(CLK), .Q(r13));  // open: en, clr
  Multiplexer #(.width(12)) multiplexer_13 (.in0(r13), .in1(D), .out(multiplexer_13_out), .sel(demultiplexer_1_out13));
  Register #(.width(12)) u_r14 (.D(multiplexer_14_out), .clk(CLK), .Q(r14));  // open: en, clr
  Multiplexer #(.width(12)) multiplexer_14 (.in0(r14), .in1(D), .out(multiplexer_14_out), .sel(demultiplexer_1_out14));
  Register #(.width(12)) u_r15 (.D(multiplexer_15_out), .clk(CLK), .Q(r15));  // open: en, clr
  Multiplexer #(.width(12)) multiplexer_15 (.in0(r15), .in1(D), .out(multiplexer_15_out), .sel(demultiplexer_1_out15));
  Multiplexer #(.select(4), .width(12)) multiplexer_16 (
    .in0({12{1'b0}}), .in1(r1), .in2(r2), .in3(r3), .in4(r4), .in5(r5), .in6(r6), .in7(r7), .in8(r8),
    .in9(r9), .in10(r10), .in11(r11), .in12(r12), .in13(r13), .in14(r14), .in15(r15), .out(a), .sel(rs1));
  Multiplexer #(.select(4), .width(12)) multiplexer_17 (
    .in0({12{1'b0}}), .in1(r1), .in2(r2), .in3(r3), .in4(r4), .in5(r5), .in6(r6), .in7(r7), .in8(r8),
    .in9(r9), .in10(r10), .in11(r11), .in12(r12), .in13(r13), .in14(r14), .in15(r15), .out(b), .sel(rs2));
endmodule

module ula (
  input  [11:0] A,
  input  [11:0] B,
  input  [3:0] OPULA,
  output Ra_igual_0,
  output [11:0] C
);

  wire [11:0] adder_1_out, and_1_out, multiplexer_1_out, multiplier_1_out, not_1_out, or_1_out,
       shifter_1_out, shifter_2_out, subtractor_1_out, xor_1_out;

  Adder #(.width(12)) adder_1 (.a(A), .b(B), .out(adder_1_out));  // open: cin, cout
  Subtractor #(.width(12)) subtractor_1 (.a(A), .b(B), .out(subtractor_1_out));  // open: bin, bout
  Multiplier #(.width(12)) multiplier_1 (.a(A), .b(B), .out(multiplier_1_out));  // open: cin, cout
  Shifter #(.width(12)) shifter_1 (.in(A), .\dist (B[3:0]), .out(shifter_1_out));
  Shifter #(.shift("lr"), .width(12)) shifter_2 (.in(A), .\dist (B[3:0]), .out(shifter_2_out));
  assign not_1_out = ~B;  // NOT_Gate not_1, 12 bits wide
  assign and_1_out = A & B;  // AND_Gate and_1, 12 bits wide
  assign or_1_out = A | B;  // OR_Gate or_1, 12 bits wide
  assign xor_1_out = A ^ B;  // XOR_Gate xor_1, 12 bits wide
  nor nor_1 (Ra_igual_0, A[0], A[1], A[2], A[3], A[4], A[5], A[6], A[7], A[8], A[9], A[10], A[11]);
  Multiplexer #(.select(3), .width(12)) multiplexer_1 (
    .in0(subtractor_1_out), .in1(multiplier_1_out), .in2(shifter_1_out), .in3(shifter_2_out),
    .in4(not_1_out), .in5(and_1_out), .in6(or_1_out), .in7(xor_1_out), .out(multiplexer_1_out),
    .sel(OPULA[2:0]));
  Multiplexer #(.width(12)) multiplexer_2 (.in0(adder_1_out), .in1(multiplexer_1_out), .out(C), .sel(OPULA[3]));
endmodule

module sel_lw (
  input  [1:0] mux_reg,
  input  clk,
  output out_3
);

  wire and_1_out, and_2_out, and_3_out, d_ff_1_q, d_ff_1_qn, xor_1_out;

  and and_1 (and_1_out, mux_reg[0], ~mux_reg[1]);  // AND_Gate
  D_Flip_Flop d_ff_1 (.D(and_2_out), .clk(clk), .Q(d_ff_1_q), .Qn(d_ff_1_qn));  // open: preset, reset
  and and_2 (and_2_out, and_1_out, d_ff_1_qn);
  xor xor_1 (xor_1_out, and_1_out, d_ff_1_q);
  Multiplexer multiplexer_1 (.in0(1'b0), .in1(xor_1_out), .out(out_3), .sel(and_3_out));
  and and_3 (and_3_out, ~mux_reg[1], mux_reg[0]);  // AND_Gate
endmodule
